// Logisim project address_decoding.circ as structural Verilog: 3 circuits, main circuit main
module main (
);

  IODEC iodec_1 ();  // open: IORQb, WRb, A0, A4, A1, A5, A2, A6, A3, A7, C2WSELb, VDPRSELb, VDPWSELb, VDPEN, C1WSELb, CRSELb, SNWSELb, AYSELb, FF1WSELb, FF2WSELb
endmodule

module IODEC (
  input  IORQb,
  input  WRb,
  input  A0,
  input  A4,
  input  A1,
  input  A5,
  input  A2,
  input  A6,
  input  A3,
  input  A7,
  output C2WSELb,
  output VDPRSELb,
  output VDPWSELb,
  output VDPEN,
  output C1WSELb,
  output CRSELb,
  output SNWSELb,
  output AYSELb,
  output FF1WSELb,
  output FF2WSELb
);

  wire and_8_out, and_9_out, and_10_out, AYSEL, C1WSEL, C2WSEL, CRSEL, FF1WSEL, FF2WSEL, IORQ, nA0, nA1, nA2,
       nA3, nA5, nA6, nA7, SNWSEL, VDPRSEL, VDPWSEL, WR;

  not not_1 (IORQ, IORQb);
  not not_2 (WR, WRb);
  not not_3 (nA0, A0);
  not not_4 (nA1, A1);
  not not_5 (nA2, A2);
  not not_6 (nA3, A3);
  and and_1 (C2WSEL, A7, nA6, nA5, IORQ, WR);
  and and_2 (VDPRSEL, A7, nA6, A5, IORQ, WRb);
  and and_3 (VDPWSEL, A7, nA6, A5, IORQ, WR);
  and and_4 (VDPEN, A7, nA6, A5, IORQ);
  and and_5 (C1WSEL, A7, A6, nA5, IORQ, WR);
  and and_6 (CRSEL, A7, A6, A5, IORQ, WRb);
  and and_7 (SNWSEL, A7, A6, A5, IORQ, WR);
  not not_7 (nA5, A5);
  not not_8 (nA6, A6);
  not not_9 (nA7, A7);
  not not_10 (C2WSELb, C2WSEL);
  LED led_1 (.in(C2WSELb));
  not not_11 (VDPRSELb, VDPRSEL);
  LED led_2 (.in(VDPRSELb));
  not not_12 (VDPWSELb, VDPWSEL);
  LED led_3 (.in(VDPWSELb));
  LED led_4 (.in(VDPEN));
  not not_13 (C1WSELb, C1WSEL);
  LED led_5 (.in(C1WSELb));
  not not_14 (CRSELb, CRSEL);
  LED led_6 (.in(CRSELb));
  not not_15 (SNWSELb, SNWSEL);
  LED led_7 (.in(SNWSELb));
  not not_16 (AYSELb, AYSEL);
  LED led_8 (.in(AYSELb));
  not not_17 (FF1WSELb, FF1WSEL);
  LED led_9 (.in(FF1WSELb));
  not not_18 (FF2WSELb, FF2WSEL);
  LED led_10 (.in(FF2WSELb));
  and and_8 (and_8_out, nA7, A6, nA5, A4, nA3, nA2, nA1, nA0, IORQ);
  and and_9 (and_9_out, nA7, A6, nA5, A4, nA3, nA2, nA1, A0, IORQ);
  and and_10 (and_10_out, nA7, A6, nA5, A4, nA3, nA2, A1, nA0, IORQ);
  or or_1 (AYSEL, and_8_out, and_9_out, and_10_out);
  and and_11 (FF1WSEL, nA7, A6, nA5, A4, nA3, nA2, A1, A0, IORQ, WR);
  and and_12 (FF2WSEL, nA7, A6, A5, A4, A3, A2, A1, A0, IORQ, WR);

  // Other names for the same wires on the sheet: nWR = WRb

  // Notes on the sheet:
  //   $8x (w)
  //   $Ax (r)
  //   $Ax (w)
  //   $Ax
  //   $Cx (w)
  //   $Ex (r)
  //   $Ex (w)
  //   $50
  //   $51
  //   $52
  //   $53 (w)
  //   $7F (w)
endmodule

module MEMDEC (
  input  MREQb,
  input  WRb,
  input  RFSHb,
  input  CLK,
  input  M1,
  input  XRAMEN,
  input  ROMEN,
  input  A13,
  input  A14,
  input  A15,
  output RAMSELb,
  output ROMSELb,
  output CRT8SELb,
  output CRTASELb,
  output CRTCSELb,
  output CRTESELb,
  output M1WAIT
);

  wire and_2_out, and_3_out, and_4_out, and_5_out, and_6_out, CRT8SEL, CRTASEL, CRTCSEL, CRTESEL, MREQ, nA13,
       nA14, nA15, not_14_out, nROMEN, RAMSEL, RFSH, ROMSEL, WR;

  not not_1 (MREQ, MREQb);
  not not_2 (WR, WRb);
  not not_3 (RFSH, RFSHb);
  not not_4 (nROMEN, ROMEN);
  not not_5 (nA13, A13);
  not not_6 (nA14, A14);
  not not_7 (nA15, A15);
  and and_1 (ROMSEL, nA13, nA13, nA13, MREQ, RFSHb, WRb, ROMEN);
  and and_2 (and_2_out, nA13, nA14, nA15, MREQ, RFSHb, WRb, nROMEN);
  and and_3 (and_3_out, nA13, nA14, nA15, MREQ, RFSHb, WR);
  and and_4 (and_4_out, A13, nA14, nA15, MREQ, RFSHb, XRAMEN);
  and and_5 (and_5_out, nA13, A14, nA15, MREQ, RFSHb, XRAMEN);
  and and_6 (and_6_out, A13, A14, nA15, MREQ, RFSHb);
  or or_1 (RAMSEL, and_2_out, and_3_out, and_4_out, and_5_out, and_6_out);
  not not_8 (RAMSELb, RAMSEL);
  LED led_1 (.in(RAMSELb));
  not not_9 (ROMSELb, ROMSEL);
  LED led_2 (.in(ROMSELb));
  not not_10 (CRT8SELb, CRT8SEL);
  LED led_3 (.in(CRT8SELb));
  not not_11 (CRTASELb, CRTASEL);
  LED led_4 (.in(CRTASELb));
  not not_12 (CRTCSELb, CRTCSEL);
  LED led_5 (.in(CRTCSELb));
  not not_13 (CRTESELb, CRTESEL);
  LED led_6 (.in(CRTESELb));
  LED led_7 (.in(M1WAIT));
  not not_14 (not_14_out, M1WAIT);
  D_Flip_Flop d_ff_1 (.D(not_14_out), .clk(CLK), .Q(M1WAIT), .reset(M1));  // open: Qn, preset
  and and_7 (CRT8SEL, nA13, nA14, A15, MREQ, RFSHb);
  and and_8 (CRTASEL, A13, nA14, A15, MREQ, RFSHb);
  and and_9 (CRTCSEL, nA13, A14, A15, MREQ, RFSHb);
  and and_10 (CRTESEL, A13, A14, A15, MREQ, RFSHb);

  // Other names for the same wires on the sheet: nRFSH = RFSHb; nWR = WRb
endmodule
